// Logisim project testerbcd.circ as structural Verilog: 1 circuit, main circuit main
module main (
);

  wire _0_1_out, _0_2_out, _0_n1_2_out, _1_n2_out, a, and_1_out, b, c, clock_1_out, d, e, f, g, n0_1_out,
       n0_2_out, n0_n1_out, n0_n2_out, n1_2_out, not_1_out, not_2_out, not_3_out, not_5_out, Reset_out, stop,
       w0, w1, w2, w3;

  not not_1 (not_1_out, w0);
  not not_2 (not_2_out, w1);
  not not_3 (not_3_out, w2);
  // NOT_Gate not_4 has open pins: in=w3, out=open
  and n0_n2 (n0_n2_out, not_1_out, not_3_out);
  and _0_2 (_0_2_out, w2, w0);
  and _1_n2 (_1_n2_out, not_3_out, w1);
  and n0_n1 (n0_n1_out, not_1_out, not_2_out);
  and _0_1 (_0_1_out, w0, w1);
  and _0_n1_2 (_0_n1_2_out, w0, w2, not_2_out);
  and n0_1 (n0_1_out, not_1_out, w1);
  or u_c (c, w0, not_2_out, w2);
  or u_a (a, w1, w3, n0_n2_out, _0_2_out);
  or u_b (b, _0_1_out, _0_1_out, not_3_out, n0_n1_out);
  or u_d (d, n0_1_out, n0_n2_out, w3, _0_n1_2_out, _1_n2_out);
  or u_e (e, n0_1_out, n0_n2_out);
  and n0_2 (n0_2_out, w2, not_1_out);
  and n1_2 (n1_2_out, w2, not_2_out);
  or u_f (f, n0_2_out, n1_2_out, n0_n1_out, w3);
  or u_g (g, n1_2_out, n0_1_out, _1_n2_out, w3);
  _7_Segment_Display u_7_segment_display_1 (.g(g), .f(f), .a(a), .b(b), .e(e), .d(d), .c(c));  // open: dp
  Clock clock_1 (.out(clock_1_out));
  // Probe on {w3, w2, w1, w0}
  and and_1 (and_1_out, clock_1_out, not_5_out);
  not not_5 (not_5_out, stop);
  TTY #(.rows(10), .cols(1)) tty_1 (.data({3'b100, d, c, b, a}), .clk(and_1_out), .clr(Reset_out));  // open: we
  Counter #(.width(4), .max('h9), .ongoal("stay")) counter_1 (
    .Q({w3, w2, w1, w0}), .carry(stop), .clk(and_1_out), .clr(Reset_out));  // open: load, D, count
  TTY #(.rows(10), .cols(1)) tty_2 (.data({4'b0110, g, f, e}), .clk(and_1_out), .clr(Reset_out));  // open: we
  Button Reset (.out(Reset_out));

  // Notes on the sheet:
  //   O
  //   F
  //   K
  //   O
  //   F
  //   M
  //   M
  //   G
  //   O
  //   3
  //   0
  //   5
  //   4
  //   6
  //   6
  //   7
  //   0
  //   7
endmodule
