// Logisim project 4bitAdder.circ as structural Verilog: 5 circuits, main circuit main
// Number Correct
module main (
  input  Enable_Halt
);

  wire and_2_out, CLK, Correct, Halt, not_1_out, not_2_out, NotDone, YourCout;
  wire [3:0] A, B, YourSum;
  wire [4:0] Solution;
  wire [8:0] Number_Correct_q;

  not not_1 (not_1_out, Correct);
  and and_1 (Halt, Enable_Halt, not_1_out);
  Clock clock_1 (.out(CLK));
  Inputs inputs_1 (.Halt(Halt), .Clk(CLK), .A(A), .B(B), .NotDone(NotDone));
  // Probe on A
  // Probe on B
  // Probe on YourSum
  // Probe on YourCout
  // Probe on Solution[3:0]
  // Probe on Solution[4]
  _4bitAdder _4BitAdder (.A(A), .B(B), .Cin(1'b0), .Sum(YourSum), .Cout(YourCout));
  not not_2 (not_2_out, Halt);
  and and_2 (and_2_out, Correct, NotDone, not_2_out);
  Checker checker_1 (.A(A), .B(B), .Sum(YourSum), .Cout(YourCout), .Correct(Correct), .CorrectAnswer(Solution));
  Counter #(.width(9), .max('h100)) Number_Correct (
    .count(and_2_out), .Q(Number_Correct_q), .clk(CLK));  // open: load, D, carry, clr
  // Probe on Number_Correct_q

  // Notes on the sheet:
  //   Use the Poke Tool on the enable halt input to enable/disable halting
  //   Enabling Halt will cause the testing to stop as soon as the first incorrect answer is detected
endmodule

module _4bitAdder (
  input  [3:0] A,
  input  [3:0] B,
  input  Cin,
  output [3:0] Sum,
  output Cout
);

  wire and_1_out, and_2_out, and_3_out, and_4_out, and_5_out, and_6_out, fulladder_1_pi, fulladder_2_gi,
       fulladder_2_pi, fulladder_3_gi, fulladder_3_pi, fulladder_4_gi, fulladder_4_pi, or_1_out, or_2_out,
       or_3_out;

  FullAdder fulladder_1 (
    .B(B[3]), .A(A[3]), .Cin(or_1_out), .Cout(Cout), .Pi(fulladder_1_pi), .Sum(Sum[3]));  // open: Gi
  and and_1 (and_1_out, fulladder_2_pi, fulladder_3_gi);
  and and_2 (and_2_out, fulladder_4_gi, fulladder_3_pi, fulladder_2_pi);
  or or_1 (or_1_out, fulladder_2_gi, and_1_out, and_2_out, and_3_out);
  FullAdder fulladder_2 (
    .B(B[2]), .A(A[2]), .Cin(or_2_out), .Gi(fulladder_2_gi), .Pi(fulladder_2_pi), .Sum(Sum[2]));  // open: Cout
  and and_3 (and_3_out, fulladder_2_pi, fulladder_3_pi, fulladder_4_pi, Cin);
  and and_4 (and_4_out, fulladder_3_pi, fulladder_4_gi);
  or or_2 (or_2_out, and_4_out, and_5_out, fulladder_3_gi);
  FullAdder fulladder_3 (
    .B(B[1]), .A(A[1]), .Cin(or_3_out), .Gi(fulladder_3_gi), .Pi(fulladder_3_pi), .Sum(Sum[1]));  // open: Cout
  and and_5 (and_5_out, Cin, fulladder_3_pi, fulladder_4_pi);
  and and_6 (and_6_out, Cin, fulladder_4_pi);
  or or_3 (or_3_out, fulladder_4_gi, and_6_out);
  FullAdder fulladder_4 (
    .B(B[0]), .A(A[0]), .Cin(Cin), .Gi(fulladder_4_gi), .Pi(fulladder_4_pi), .Sum(Sum[0]));  // open: Cout
endmodule

module Inputs (
  input  Halt,
  input  Clk,
  output [3:0] A,
  output [3:0] B,
  output NotDone
);

  wire A_carry, and_1_out, and_2_out, and_3_out, and_4_out, CarryB, Delay_q, nHalt;

  not not_1 (nHalt, Halt);
  and and_1 (and_1_out, nHalt, NotDone);
  Counter #(.width(4), .max('hf)) u_B (.count(and_1_out), .Q(B), .carry(CarryB), .clk(Clk));  // open: load, D, clr
  and and_2 (and_2_out, nHalt, CarryB);
  Counter #(.width(4), .max('hf), .ongoal("stay")) u_A (
    .count(and_2_out), .Q(A), .carry(A_carry), .clk(Clk));  // open: load, D, clr
  and and_3 (and_3_out, CarryB, A_carry);
  Register #(.width(1)) Delay (.D(and_3_out), .en(and_4_out), .Q(Delay_q), .clk(Clk));  // open: clr
  and and_4 (and_4_out, nHalt, NotDone);
  not not_2 (NotDone, Delay_q);
endmodule

module Checker (
  input  [3:0] A,
  input  [3:0] B,
  input  [3:0] Sum,
  input  Cout,
  output Correct,
  output [4:0] CorrectAnswer
);

  ROM #(.dataWidth(5)) rom_1 (.addr({A, B}), .data(CorrectAnswer));  // open: sel
  Comparator #(.width(5), .mode("unsigned")) comparator_1 (
    .a(CorrectAnswer), .b({Cout, Sum}), .eq(Correct));  // open: gt, lt

  // Other names for the same wires on the sheet: StudentSol[4:0] = {Cout, Sum}

  // Notes on the sheet:
  //   contents of rom_1 (hex, n*v repeats v):
  //   0 1 2 3 4 5 6 7 8 9 a b c d e f 1 2 3 4 5 6 7 8 9 a b c d e f 10 2 3 4 5 6 7 8 9 a b c d e f 10 11 3
  //   4 5 6 7 8 9 a b c d e f 10 11 12 4 5 6 7 8 9 a b c d e f 10 11 12 13 5 6 7 8 9 a b c d e f 10 11 12
  //   13 14 6 7 8 9 a b c d e f 10 11 12 13 14 15 7 8 9 a b c d e f 10 11 12 13 14 15 16 8 9 a b c d e f
  //   10 11 12 13 14 15 16 17 9 a b c d e f 10 11 12 13 14 15 16 17 18 a b c d e f 10 11 12 13 14 15 16 17
  //   18 19 b c d e f 10 11 12 13 14 15 16 17 18 19 1a c d e f 10 11 12 13 14 15 16 17 18 19 1a 1b d e f
  //   10 11 12 13 14 15 16 17 18 19 1a 1b 1c e f 10 11 12 13 14 15 16 17 18 19 1a 1b 1c 1d f 10 11 12 13
  //   14 15 16 17 18 19 1a 1b 1c 1d 1e
endmodule

module FullAdder (
  input  B,
  input  A,
  input  Cin,
  output Gi,
  output Pi,
  output Cout,
  output Sum
);

  wire and_2_out;

  and and_1 (Gi, B, A);
  xor xor_1 (Pi, B, A);
  and and_2 (and_2_out, Cin, Pi);
  xor xor_2 (Sum, Pi, Cin);
  or or_1 (Cout, Gi, and_2_out);
endmodule
