// Logisim project Written HW Logisim Circuits.circ as structural Verilog
module _8_1_MUX (
  input  x2,
  input  in_2,
  input  in_3,
  input  x1,
  input  in_5,
  input  in_6,
  input  x0,
  input  in_8,
  input  in_9,
  input  in_10,
  input  [2:0] in_11,
  input  in_12,
  input  in_13,
  input  in_14,
  input  in_15,
  input  [2:0] in_16,
  input  in_17,
  input  in_18,
  input  in_19,
  input  in_20,
  output F,
  output out_22,
  output out_23
);

  wire and_1_out, and_2_out, and_3_out, and_4_out, decoder_1_out0, decoder_1_out2, decoder_1_out6,
       multiplexer_2_out, multiplexer_3_out, multiplexer_4_out, multiplexer_5_out, multiplexer_6_out,
       multiplexer_7_out, not_1_out, not_2_out, not_3_out, not_4_out;

  Decoder #(.select(3)) decoder_1 (
    .out0(decoder_1_out0), .out2(decoder_1_out2), .out6(decoder_1_out6), .sel(in_11));  // open: out1, out3, out4, out5, out7, en
  not not_1 (not_1_out, x2);
  not not_2 (not_2_out, x0);
  not not_3 (not_3_out, x1);
  not not_4 (not_4_out, x0);
  and and_1 (and_1_out, not_1_out, x1, not_2_out);
  and and_2 (and_2_out, x2, not_3_out, x0);
  and and_3 (and_3_out, x2, x1, not_4_out);
  and and_4 (and_4_out, x2, x1, x0);
  Multiplexer #(.select(3)) multiplexer_1 (
    .in0(in_20), .in1(in_20), .in2(in_20), .in3(in_17), .in4(in_20), .in5(in_17), .in6(in_17), .in7(in_17),
    .out(in_19), .sel(in_16), .en(in_18));
  or or_1 (F, and_1_out, and_2_out, and_3_out, and_4_out);
  or or_2 (out_23, decoder_1_out0, decoder_1_out2, decoder_1_out6);
  Multiplexer multiplexer_2 (.in0(in_6), .in1(in_8), .out(multiplexer_2_out), .sel(in_2));  // open: en
  Multiplexer multiplexer_3 (.in0(in_9), .in1(in_10), .out(multiplexer_3_out), .sel(in_2));  // open: en
  Multiplexer multiplexer_4 (.in0(in_12), .in1(in_13), .out(multiplexer_4_out), .sel(in_2));  // open: en
  Multiplexer multiplexer_5 (.in0(in_14), .in1(in_15), .out(multiplexer_5_out), .sel(in_2));  // open: en
  Multiplexer multiplexer_6 (
    .in0(multiplexer_2_out), .in1(multiplexer_3_out), .out(multiplexer_6_out), .sel(in_3));  // open: en
  Multiplexer multiplexer_7 (
    .in0(multiplexer_4_out), .in1(multiplexer_5_out), .out(multiplexer_7_out), .sel(in_3));  // open: en
  Multiplexer multiplexer_8 (.in0(multiplexer_6_out), .in1(multiplexer_7_out), .out(out_22), .sel(in_5));  // open: en

  // Other names for the same wires on the sheet: S0 = in_2; S1 = in_3; S2 = in_5; X0_t = in_6; X1_t = in_8;
  //   X2_t = in_9; X3 = in_10; X4 = in_12; X5 = in_13; X6 = in_14; X7 = in_15
endmodule
